# Fritzing sketch Arduino-Sketch (saved by Fritzing 0.9.10b)

parts:
  Part1 = Arduino Mega 2560 (Rev3)
  Part2 = NRF24L01+ Breakout Board

nets:
  N1: Part1.D8_PWM, Part2.CS
  3V3: Part1.3V3, Part2.VCC
  GND: Part1.GND, Part2.GND
  N2: Part1.D7_PWM, Part2.CE
  N3: Part1.D50, Part2.MISO
  N4: Part1.D51, Part2.MOSI
  N5: Part1.D52, Part2.SCK

notes:
  Power and Grownd from power managment board
  Power off button to Power managment board
