# Fritzing sketch Raspberry-Sketch (saved by Fritzing 0.9.10b)

parts:
  Raspberry_Pi_1 = Raspberry Pi 3 [part_number=RPI-3-V1.2]
  Part1 = NRF24L01+ Breakout Board

nets:
  3V3: Raspberry_Pi_1.3v3, Part1.VCC
  N1: Raspberry_Pi_1.GPIO17, Part1.CE
  N2: Raspberry_Pi_1.GPIO10, Part1.MOSI
  N3: Raspberry_Pi_1.GPIO9, Part1.MISO
  N4: Raspberry_Pi_1.GPIO11, Part1.SCK
  N5: Raspberry_Pi_1.GPIO8, Part1.CS
  GND: Raspberry_Pi_1.GND, Part1.GND
